# Fritzing sketch RRLCar_Able (saved by Fritzing 0.9.2b)

parts:
  Parte1 = Arduino Uno (Rev3)
  U1 = L298 [package=multiwatt15]  # not connected
  U2 = 74HC595 SMD [package="SO16 [SMD]"]  # not connected
  LED1 = smd LED [color="Red (633nm)" package="0603 [SMD]"]  # not connected
  LED2 = smd LED [color="Red (633nm)" package="0603 [SMD]"]  # not connected
  LED3 = smd LED [color="Red (633nm)" package="0603 [SMD]"]  # not connected
  LED4 = smd LED [color="Red (633nm)" package="0603 [SMD]"]  # not connected
  LED5 = smd LED [color="Red (633nm)" package="0603 [SMD]"]  # not connected
  LED6 = smd LED [color="Red (633nm)" package="0603 [SMD]"]  # not connected
  LED7 = smd LED [color="Red (633nm)" package="0603 [SMD]"]  # not connected
  LED8 = smd LED [color="Red (633nm)" package="0603 [SMD]"]  # not connected
  J1 = Piezo Speaker

nets:
  N1: Parte1.D11_PWM/MOSI, J1.pin2
  N2: Parte1.GND, J1.pin1
